# Fritzing sketch chickenpi (saved by Fritzing 0.9.3b)
breadboards: 1

parts:
  Raspberry_Pi2 = Raspberry Pi 2
  S2 = H-Bridge with L298N
  VCC2 = 4 x AAA Battery Mount
  coop_door_motor = DC Motor
  U1 = Module 4 Relais 5V [package="Module 4 Relais 5V"]
  DS1 = DS18B20 1-Wire Temperature Sensor [part_number=DS18B20]
  DS2 = DS18B20 1-Wire Temperature Sensor [part_number=DS18B20]
  R1 = Resistor [tolerance=±5% resistance=3.3k package="2010 [SMD]"]

nets:
  VDD: Raspberry_Pi2.3v3, U1.VCC, DS1.VDD, DS2.VDD, R1.Pin_0
  N1: Raspberry_Pi2.GPIO4, DS1.DQ, DS2.DQ, R1.Pin_1
  N2: Raspberry_Pi2.GPIO17, U1.IN1
  N3: Raspberry_Pi2.GPIO27, S2.IN2
  GND: Raspberry_Pi2.GND, S2.GND, VCC2.-, U1.GND, DS1.GND, DS2.GND
  N4: Raspberry_Pi2.GPIO24, S2.IN1
  N5: Raspberry_Pi2.GPIO23, S2.ENA
  N6: Raspberry_Pi2.5V, U1.JD-VCC
  N7: S2.12V, VCC2.+
  N8: S2.M1-01, coop_door_motor.pin_2
  N9: S2.M1-02, coop_door_motor.pin_1

notes:
  orange 3V
  red 5V
  yellow ground
  green motor A on
  brown motor A up
  white motor A down
  mangenta toggle light 1
  cyan temperature
  relays for lights
  coop door power
  coop door motor
  temperature sensors
  motor driver

custom parts:
  H-Bridge with L298N: h-bridge
  Module 4 Relais 5V: Module 4 Relais 5V 4x SPD-06VDC-SD-C
